// Logisim project cpu.circ as structural Verilog: 15 circuits, main circuit main
module main (
  input  reset
);

  wire ALUinB, and_1_out, and_2_out, blt, bne, clk, DMWe, fclk, \input , jal, JP, jr, keyboard_1_avail,
       lessThan, neq, \output , Rdst, RWd, RWE;
  wire [2:0] ALUop, instruction_decode_1_rd, instruction_decode_1_rs, instruction_decode_1_rt,
       multiplexer_4_out, multiplexer_5_out, shamt;
  wire [3:0] instruction_decode_1_opcode;
  wire [5:0] instruction_decode_1_immediate;
  wire [6:0] displayformatter_1_formatted_display, keyboard_1_data;
  wire [11:0] instruction_decode_1_address;
  wire [15:0] adder_1_result, adder_2_result, Addr, alu_1_out, bit_extender_1_out, Imm, KeyboardRd,
       multiplexer_1_out, multiplexer_2_out, multiplexer_3_out, multiplexer_6_out, multiplexer_7_out,
       multiplexer_8_out, multiplexer_9_out, multiplexer_10_out, multiplexer_11_out, PC, pc_1, r1val,
       ram_1_data, registerfile_1_readdata1_2, rom_1_data;

  pc_1 pc_1_1 (.pc(PC), .pc_4(pc_1));
  register u_PC (.Input(multiplexer_8_out), .clk(clk), .WriteEnable(1'b1), .Reset(reset), .Output(PC));
  Clock clock_1 (.out(clk));
  not not_1 (fclk, clk);
  Multiplexer #(.width(16), .disabled(0), .enable("false")) multiplexer_1 (
    .in0(pc_1), .in1(Addr), .out(multiplexer_1_out), .sel(JP));
  ROM #(.addrWidth(16), .dataWidth(16)) rom_1 (.addr(PC), .data(rom_1_data));  // open: sel
  Multiplexer #(.width(16), .disabled(0), .enable("false")) multiplexer_2 (
    .in0(multiplexer_1_out), .in1(r1val), .out(multiplexer_2_out), .sel(jr));
  control control_1 (
    .Opcode(instruction_decode_1_opcode), .ALUop(ALUop), .RWE(RWE), .ALUinB(ALUinB), .DMWe(DMWe), .RWd(RWd),
    .Rdst(Rdst), .JP(JP), .\input (\input ), .\output (\output ), .jal(jal), .jr(jr), .bne(bne), .blt(blt));
  Multiplexer #(.width(16), .disabled(0), .enable("false")) multiplexer_3 (
    .in0(multiplexer_2_out), .in1(Addr), .out(multiplexer_3_out), .sel(jal));
  Multiplexer #(.width(3), .disabled(0), .enable("false")) multiplexer_4 (
    .in0(multiplexer_5_out), .in1(3'b111), .out(multiplexer_4_out), .sel(jal));
  Multiplexer #(.width(3), .disabled(0), .enable("false")) multiplexer_5 (
    .in0(instruction_decode_1_rt), .in1(instruction_decode_1_rd), .out(multiplexer_5_out), .sel(Rdst));
  Keyboard keyboard_1 (.clk(clk), .re(\input ), .clr(reset), .avail(keyboard_1_avail), .data(keyboard_1_data));
  adder adder_1 (.B(multiplexer_3_out), .sub(1'b0), .A(Imm), .result(adder_1_result));  // open: ovf
  RegisterFile registerfile_1 (
    .Reset(reset), .ReadReg1(instruction_decode_1_rs), .ReadReg2(instruction_decode_1_rt),
    .RegWriteEnable(RWE), .WriteReg(multiplexer_4_out), .clk(fclk), .WriteData(multiplexer_11_out),
    .ReadData1(r1val), .ReadData1_2(registerfile_1_readdata1_2));
  inputReader inputreader_1 (.read_Input(keyboard_1_data), .Available(keyboard_1_avail), .Formatted_Read(KeyboardRd));
  Multiplexer #(.width(16), .disabled(0), .enable("false")) multiplexer_6 (
    .in0(multiplexer_3_out), .in1(adder_1_result), .out(multiplexer_6_out), .sel(and_1_out));
  and and_1 (and_1_out, neq, bne);
  assign bit_extender_1_out = {{4{1'b0}}, instruction_decode_1_address};  // Bit_Extender bit_extender_1
  assign Imm = {{10{instruction_decode_1_immediate[5]}}, instruction_decode_1_immediate};  // Bit_Extender bit_extender_2
  Instruction_Decode instruction_decode_1 (
    .instruction(rom_1_data), .Address(instruction_decode_1_address),
    .Immediate(instruction_decode_1_immediate), .shamt(shamt), .Rd(instruction_decode_1_rd),
    .Rt(instruction_decode_1_rt), .Rs(instruction_decode_1_rs), .opcode(instruction_decode_1_opcode));
  adder adder_2 (.B(multiplexer_6_out), .sub(1'b0), .A(Imm), .result(adder_2_result));  // open: ovf
  Multiplexer #(.width(16), .disabled(0), .enable("false")) multiplexer_7 (
    .in0(registerfile_1_readdata1_2), .in1(Imm), .out(multiplexer_7_out), .sel(ALUinB));
  address_manipulator address_manipulator_1 (.addr12(bit_extender_1_out), .PC(PC), .out_3(Addr));
  displayformatter displayformatter_1 (.rs(r1val), .formatted_display(displayformatter_1_formatted_display));
  and and_2 (and_2_out, lessThan, blt);
  TTY #(.rows(13), .cols(80), .trigger("falling")) tty_1 (
    .data(displayformatter_1_formatted_display), .clk(fclk), .we(\output ), .clr(reset));
  Multiplexer #(.width(16), .disabled(0), .enable("false")) multiplexer_8 (
    .in0(multiplexer_6_out), .in1(adder_2_result), .out(multiplexer_8_out), .sel(and_2_out));
  ALU alu_1 (
    .a(r1val), .b(multiplexer_7_out), .shamt(shamt), .ALUop(ALUop), .out(alu_1_out), .bne(neq), .blt(lessThan));
  RAM #(.addrWidth(16), .dataWidth(16), .bus("separate")) ram_1 (
    .addr(alu_1_out), .din(registerfile_1_readdata1_2), .data(ram_1_data), .str(DMWe), .clk(fclk));  // open: sel, ld, clr
  Multiplexer #(.width(16), .disabled(0), .enable("false")) multiplexer_9 (
    .in0(alu_1_out), .in1(ram_1_data), .out(multiplexer_9_out), .sel(RWd));
  Multiplexer #(.width(16), .disabled(0), .enable("false")) multiplexer_10 (
    .in0(multiplexer_9_out), .in1(pc_1), .out(multiplexer_10_out), .sel(jal));
  Multiplexer #(.width(16), .disabled(0), .enable("false")) multiplexer_11 (
    .in0(multiplexer_10_out), .in1(KeyboardRd), .out(multiplexer_11_out), .sel(\input ));

  // Other names for the same wires on the sheet: R = reset

  // Notes on the sheet:
  //   contents of rom_1 (hex, n*v repeats v):
  //   104f 1090 10ca a457 a284 1194 91ff 1fc1 91ff d010 92d0 920a 1195 91ff 1fc1 91ff 127b ce00 1196 91ff
  //   1fc1 91ff b018 1197 91ff 1fc1 91ff 1198 91ff 1fc1 91ff
endmodule

module RegisterFile (
  input  Reset,
  input  [2:0] ReadReg1,
  input  [2:0] ReadReg2,
  input  RegWriteEnable,
  input  [2:0] WriteReg,
  input  clk,
  input  [15:0] WriteData,
  output [15:0] ReadData1,
  output [15:0] ReadData1_2
);

  wire decoder_1_out1, decoder_1_out2, decoder_1_out3, decoder_1_out4, decoder_1_out5, decoder_1_out6,
       decoder_1_out7;
  wire [15:0] register_1_output, register_2_output, register_3_output, register_4_output, register_5_output,
       register_6_output, register_7_output;

  Decoder #(.select(3), .disabled(0)) decoder_1 (
    .out1(decoder_1_out1), .out2(decoder_1_out2), .out3(decoder_1_out3), .out4(decoder_1_out4),
    .out5(decoder_1_out5), .out6(decoder_1_out6), .out7(decoder_1_out7), .sel(WriteReg), .en(RegWriteEnable));  // open: out0
  register register_1 (
    .Input(WriteData), .clk(clk), .WriteEnable(decoder_1_out1), .Reset(Reset), .Output(register_1_output));
  register register_2 (
    .Input(WriteData), .clk(clk), .WriteEnable(decoder_1_out2), .Reset(Reset), .Output(register_2_output));
  register register_3 (
    .Input(WriteData), .clk(clk), .WriteEnable(decoder_1_out3), .Reset(Reset), .Output(register_3_output));
  register register_4 (
    .Input(WriteData), .clk(clk), .WriteEnable(decoder_1_out4), .Reset(Reset), .Output(register_4_output));
  register register_5 (
    .Input(WriteData), .clk(clk), .WriteEnable(decoder_1_out5), .Reset(Reset), .Output(register_5_output));
  register register_6 (
    .Input(WriteData), .clk(clk), .WriteEnable(decoder_1_out6), .Reset(Reset), .Output(register_6_output));
  register register_7 (
    .Input(WriteData), .clk(clk), .WriteEnable(decoder_1_out7), .Reset(Reset), .Output(register_7_output));
  // Probe on register_1_output
  // Probe on register_2_output
  // Probe on register_3_output
  // Probe on register_4_output
  // Probe on register_5_output
  // Probe on register_6_output
  // Probe on register_7_output
  // Probe on {16{1'b0}}
  decoder_tristate decoder_tristate_1 (
    .In1({16{1'b0}}), .In2(register_1_output), .In3(register_2_output), .In4(register_3_output),
    .In5(register_4_output), .In6(register_5_output), .In7(register_6_output), .In8(register_7_output),
    .select(ReadReg1), .Out(ReadData1));
  decoder_tristate decoder_tristate_2 (
    .In1({16{1'b0}}), .In2(register_1_output), .In3(register_2_output), .In4(register_3_output),
    .In5(register_4_output), .In6(register_5_output), .In7(register_6_output), .In8(register_7_output),
    .select(ReadReg2), .Out(ReadData1_2));

  // Other names for the same wires on the sheet: R1[2:0] = ReadReg1; R2[2:0] = ReadReg2
endmodule

module register (
  input  [15:0] Input,
  input  clk,
  input  WriteEnable,
  input  Reset,
  output [15:0] Output
);

  D_Flip_Flop d_ff_1 (.clk(clk), .D(Input[0]), .Q(Output[0]), .en(WriteEnable), .reset(Reset));  // open: Qn, preset
  D_Flip_Flop d_ff_2 (.clk(clk), .D(Input[1]), .Q(Output[1]), .en(WriteEnable), .reset(Reset));  // open: Qn, preset
  D_Flip_Flop d_ff_3 (.clk(clk), .D(Input[2]), .Q(Output[2]), .en(WriteEnable), .reset(Reset));  // open: Qn, preset
  D_Flip_Flop d_ff_4 (.clk(clk), .D(Input[3]), .Q(Output[3]), .en(WriteEnable), .reset(Reset));  // open: Qn, preset
  D_Flip_Flop d_ff_5 (.clk(clk), .D(Input[4]), .Q(Output[4]), .en(WriteEnable), .reset(Reset));  // open: Qn, preset
  D_Flip_Flop d_ff_6 (.clk(clk), .D(Input[5]), .Q(Output[5]), .en(WriteEnable), .reset(Reset));  // open: Qn, preset
  D_Flip_Flop d_ff_7 (.clk(clk), .D(Input[6]), .Q(Output[6]), .en(WriteEnable), .reset(Reset));  // open: Qn, preset
  D_Flip_Flop d_ff_8 (.clk(clk), .D(Input[7]), .Q(Output[7]), .en(WriteEnable), .reset(Reset));  // open: Qn, preset
  D_Flip_Flop d_ff_9 (.clk(clk), .D(Input[8]), .Q(Output[8]), .en(WriteEnable), .reset(Reset));  // open: Qn, preset
  D_Flip_Flop d_ff_10 (.clk(clk), .D(Input[9]), .Q(Output[9]), .en(WriteEnable), .reset(Reset));  // open: Qn, preset
  D_Flip_Flop d_ff_11 (.clk(clk), .D(Input[10]), .Q(Output[10]), .en(WriteEnable), .reset(Reset));  // open: Qn, preset
  D_Flip_Flop d_ff_12 (.clk(clk), .D(Input[11]), .Q(Output[11]), .en(WriteEnable), .reset(Reset));  // open: Qn, preset
  D_Flip_Flop d_ff_13 (.clk(clk), .D(Input[12]), .Q(Output[12]), .en(WriteEnable), .reset(Reset));  // open: Qn, preset
  D_Flip_Flop d_ff_14 (.clk(clk), .D(Input[13]), .Q(Output[13]), .en(WriteEnable), .reset(Reset));  // open: Qn, preset
  D_Flip_Flop d_ff_15 (.clk(clk), .D(Input[14]), .Q(Output[14]), .en(WriteEnable), .reset(Reset));  // open: Qn, preset
  D_Flip_Flop d_ff_16 (.clk(clk), .D(Input[15]), .Q(Output[15]), .en(WriteEnable), .reset(Reset));  // open: Qn, preset

  // Other names for the same wires on the sheet: R = Reset; WE = WriteEnable
endmodule

module decoder_tristate (
  input  [15:0] In1,
  input  [15:0] In2,
  input  [15:0] In3,
  input  [2:0] select,
  input  [15:0] In4,
  input  [15:0] In5,
  input  [15:0] In6,
  input  [15:0] In7,
  input  [15:0] In8,
  output [15:0] Out
);

  wire decoder_1_out0, decoder_1_out1, decoder_1_out2, decoder_1_out3, decoder_1_out4, decoder_1_out5,
       decoder_1_out6, decoder_1_out7;

  assign Out = decoder_1_out0 ? In1 : 16'bz;  // Controlled_Buffer controlled_buffer_1
  assign Out = decoder_1_out1 ? In2 : 16'bz;  // Controlled_Buffer controlled_buffer_2
  assign Out = decoder_1_out2 ? In3 : 16'bz;  // Controlled_Buffer controlled_buffer_3
  assign Out = decoder_1_out3 ? In4 : 16'bz;  // Controlled_Buffer controlled_buffer_4
  assign Out = decoder_1_out4 ? In5 : 16'bz;  // Controlled_Buffer controlled_buffer_5
  assign Out = decoder_1_out5 ? In6 : 16'bz;  // Controlled_Buffer controlled_buffer_6
  assign Out = decoder_1_out6 ? In7 : 16'bz;  // Controlled_Buffer controlled_buffer_7
  assign Out = decoder_1_out7 ? In8 : 16'bz;  // Controlled_Buffer controlled_buffer_8
  Decoder #(.select(3), .disabled(0), .enable("false")) decoder_1 (
    .out0(decoder_1_out0), .out1(decoder_1_out1), .out2(decoder_1_out2), .out3(decoder_1_out3),
    .out4(decoder_1_out4), .out5(decoder_1_out5), .out6(decoder_1_out6), .out7(decoder_1_out7), .sel(select));
endmodule

module ALU (
  input  [15:0] a,
  input  [15:0] b,
  input  [2:0] shamt,
  input  [2:0] ALUop,
  output bne,
  output [15:0] out,
  output blt
);

  wire [14:0] SUB_result;
  wire [15:0] ADD_result, NOT_out, SLL_out, SRL_out, XOR_out;

  adder ADD (.B(b), .sub(1'b0), .A(a), .result(ADD_result));  // open: ovf
  adder SUB (.B(b), .sub(1'b1), .A(a), .result({blt, SUB_result}));  // open: ovf
  assign NOT_out = ~a;  // NOT_Gate NOT, 16 bits wide
  left_logical_shift SLL (.shift_by(shamt), .in(a), .out(SLL_out));
  right_logical_shift SRL (.shift_by(shamt), .in(a), .out(SRL_out));
  assign XOR_out = a ^ b;  // XOR_Gate XOR, 16 bits wide
  Multiplexer #(.select(3), .width(16), .disabled(0)) multiplexer_1 (
    .in0(ADD_result), .in1({blt, SUB_result}), .in2(NOT_out), .in3(XOR_out), .in4(SLL_out), .in5(SRL_out),
    .out(out), .sel(ALUop), .en(1'b1));  // open: in6, in7
  or or_1 (bne, SUB_result[0], SUB_result[1], SUB_result[2], SUB_result[3], SUB_result[4], SUB_result[5], SUB_result[6], SUB_result[7], SUB_result[8], SUB_result[9], SUB_result[10], SUB_result[11], SUB_result[12], SUB_result[13], SUB_result[14], blt, 1'b0);

  // Other names for the same wires on the sheet: op[2:0] = ALUop; shift[2:0] = shamt
endmodule

module _1_bit_full_adder (
  input  Cin,
  input  a,
  input  b,
  output Sum,
  output Cout
);

  wire and_1_out, and_2_out, xor_1_out;

  and and_1 (and_1_out, b, a);
  xor xor_1 (xor_1_out, a, b);
  or or_1 (Cout, and_1_out, and_2_out);
  and and_2 (and_2_out, xor_1_out, Cin);
  xor xor_2 (Sum, Cin, xor_1_out);
endmodule

module adder (
  input  [15:0] B,
  input  sub,
  input  [15:0] A,
  output ovf,
  output [15:0] result
);

  wire n1_bit_full_adder_1_cout, n1_bit_full_adder_2_cout, n1_bit_full_adder_3_cout,
       n1_bit_full_adder_4_cout, n1_bit_full_adder_5_cout, n1_bit_full_adder_6_cout,
       n1_bit_full_adder_7_cout, n1_bit_full_adder_8_cout, n1_bit_full_adder_9_cout,
       n1_bit_full_adder_10_cout, n1_bit_full_adder_11_cout, n1_bit_full_adder_12_cout,
       n1_bit_full_adder_13_cout, n1_bit_full_adder_14_cout, n1_bit_full_adder_15_cout,
       n1_bit_full_adder_16_cout, xor_2_out, xor_3_out, xor_4_out, xor_5_out, xor_6_out, xor_7_out,
       xor_8_out, xor_9_out, xor_10_out, xor_11_out, xor_12_out, xor_13_out, xor_14_out, xor_15_out,
       xor_16_out, xor_17_out;

  xor xor_1 (ovf, n1_bit_full_adder_1_cout, n1_bit_full_adder_2_cout);
  xor xor_2 (xor_2_out, sub, B[15]);
  _1_bit_full_adder u_1_bit_full_adder_1 (
    .Cin(n1_bit_full_adder_2_cout), .a(A[15]), .b(xor_2_out), .Cout(n1_bit_full_adder_1_cout),
    .Sum(result[15]));
  xor xor_3 (xor_3_out, sub, B[14]);
  _1_bit_full_adder u_1_bit_full_adder_2 (
    .Cin(n1_bit_full_adder_3_cout), .a(A[14]), .b(xor_3_out), .Cout(n1_bit_full_adder_2_cout),
    .Sum(result[14]));
  xor xor_4 (xor_4_out, sub, B[13]);
  _1_bit_full_adder u_1_bit_full_adder_3 (
    .Cin(n1_bit_full_adder_4_cout), .a(A[13]), .b(xor_4_out), .Cout(n1_bit_full_adder_3_cout),
    .Sum(result[13]));
  xor xor_5 (xor_5_out, sub, B[11]);
  xor xor_6 (xor_6_out, sub, B[12]);
  _1_bit_full_adder u_1_bit_full_adder_4 (
    .Cin(n1_bit_full_adder_6_cout), .a(A[12]), .b(xor_6_out), .Cout(n1_bit_full_adder_4_cout),
    .Sum(result[12]));
  xor xor_7 (xor_7_out, sub, B[10]);
  _1_bit_full_adder u_1_bit_full_adder_5 (
    .Cin(n1_bit_full_adder_7_cout), .a(A[10]), .b(xor_7_out), .Cout(n1_bit_full_adder_5_cout),
    .Sum(result[10]));
  _1_bit_full_adder u_1_bit_full_adder_6 (
    .Cin(n1_bit_full_adder_5_cout), .a(A[11]), .b(xor_5_out), .Cout(n1_bit_full_adder_6_cout),
    .Sum(result[11]));
  xor xor_8 (xor_8_out, sub, B[9]);
  _1_bit_full_adder u_1_bit_full_adder_7 (
    .Cin(n1_bit_full_adder_8_cout), .a(A[9]), .b(xor_8_out), .Cout(n1_bit_full_adder_7_cout), .Sum(result[9]));
  xor xor_9 (xor_9_out, sub, B[8]);
  _1_bit_full_adder u_1_bit_full_adder_8 (
    .Cin(n1_bit_full_adder_9_cout), .a(A[8]), .b(xor_9_out), .Cout(n1_bit_full_adder_8_cout), .Sum(result[8]));
  xor xor_10 (xor_10_out, sub, B[6]);
  xor xor_11 (xor_11_out, sub, B[7]);
  _1_bit_full_adder u_1_bit_full_adder_9 (
    .Cin(n1_bit_full_adder_10_cout), .a(A[7]), .b(xor_11_out), .Cout(n1_bit_full_adder_9_cout),
    .Sum(result[7]));
  xor xor_12 (xor_12_out, sub, B[5]);
  _1_bit_full_adder u_1_bit_full_adder_10 (
    .Cin(n1_bit_full_adder_11_cout), .a(A[6]), .b(xor_10_out), .Cout(n1_bit_full_adder_10_cout),
    .Sum(result[6]));
  _1_bit_full_adder u_1_bit_full_adder_11 (
    .Cin(n1_bit_full_adder_12_cout), .a(A[5]), .b(xor_12_out), .Cout(n1_bit_full_adder_11_cout),
    .Sum(result[5]));
  xor xor_13 (xor_13_out, sub, B[4]);
  _1_bit_full_adder u_1_bit_full_adder_12 (
    .Cin(n1_bit_full_adder_13_cout), .a(A[4]), .b(xor_13_out), .Cout(n1_bit_full_adder_12_cout),
    .Sum(result[4]));
  xor xor_14 (xor_14_out, sub, B[3]);
  _1_bit_full_adder u_1_bit_full_adder_13 (
    .Cin(n1_bit_full_adder_14_cout), .a(A[3]), .b(xor_14_out), .Cout(n1_bit_full_adder_13_cout),
    .Sum(result[3]));
  xor xor_15 (xor_15_out, sub, B[2]);
  _1_bit_full_adder u_1_bit_full_adder_14 (
    .Cin(n1_bit_full_adder_15_cout), .a(A[2]), .b(xor_15_out), .Cout(n1_bit_full_adder_14_cout),
    .Sum(result[2]));
  xor xor_16 (xor_16_out, sub, B[1]);
  _1_bit_full_adder u_1_bit_full_adder_15 (
    .Cin(n1_bit_full_adder_16_cout), .a(A[1]), .b(xor_16_out), .Cout(n1_bit_full_adder_15_cout),
    .Sum(result[1]));
  xor xor_17 (xor_17_out, sub, B[0]);
  _1_bit_full_adder u_1_bit_full_adder_16 (
    .Cin(sub), .a(A[0]), .b(xor_17_out), .Cout(n1_bit_full_adder_16_cout), .Sum(result[0]));
endmodule

module right_logical_shift (
  input  [2:0] shift_by,
  input  [15:0] in,
  output [15:0] out
);

  wire multiplexer_1_out, multiplexer_2_out, multiplexer_3_out, multiplexer_4_out, multiplexer_5_out,
       multiplexer_6_out, multiplexer_7_out, multiplexer_8_out, multiplexer_9_out, multiplexer_10_out,
       multiplexer_11_out, multiplexer_12_out, multiplexer_13_out, multiplexer_14_out, multiplexer_15_out,
       multiplexer_16_out, multiplexer_17_out, multiplexer_18_out, multiplexer_19_out, multiplexer_20_out,
       multiplexer_21_out, multiplexer_22_out, multiplexer_23_out, multiplexer_24_out, multiplexer_25_out,
       multiplexer_26_out, multiplexer_27_out, multiplexer_28_out, multiplexer_29_out, multiplexer_30_out,
       multiplexer_31_out, multiplexer_32_out;

  Multiplexer #(.disabled(0), .enable("false")) multiplexer_1 (
    .in0(in[0]), .in1(in[4]), .out(multiplexer_1_out), .sel(shift_by[2]));
  Multiplexer #(.disabled(0), .enable("false")) multiplexer_2 (
    .in0(in[1]), .in1(in[5]), .out(multiplexer_2_out), .sel(shift_by[2]));
  Multiplexer #(.disabled(0), .enable("false")) multiplexer_3 (
    .in0(in[2]), .in1(in[6]), .out(multiplexer_3_out), .sel(shift_by[2]));
  Multiplexer #(.disabled(0), .enable("false")) multiplexer_4 (
    .in0(in[3]), .in1(in[7]), .out(multiplexer_4_out), .sel(shift_by[2]));
  Multiplexer #(.disabled(0), .enable("false")) multiplexer_5 (
    .in0(in[4]), .in1(in[8]), .out(multiplexer_5_out), .sel(shift_by[2]));
  Multiplexer #(.disabled(0), .enable("false")) multiplexer_6 (
    .in0(in[5]), .in1(in[9]), .out(multiplexer_6_out), .sel(shift_by[2]));
  Multiplexer #(.disabled(0), .enable("false")) multiplexer_7 (
    .in0(in[6]), .in1(in[10]), .out(multiplexer_7_out), .sel(shift_by[2]));
  Multiplexer #(.disabled(0), .enable("false")) multiplexer_8 (
    .in0(in[7]), .in1(in[11]), .out(multiplexer_8_out), .sel(shift_by[2]));
  Multiplexer #(.disabled(0), .enable("false")) multiplexer_9 (
    .in0(in[8]), .in1(in[12]), .out(multiplexer_9_out), .sel(shift_by[2]));
  Multiplexer #(.disabled(0), .enable("false")) multiplexer_10 (
    .in0(in[9]), .in1(in[13]), .out(multiplexer_10_out), .sel(shift_by[2]));
  Multiplexer #(.disabled(0), .enable("false")) multiplexer_11 (
    .in0(in[10]), .in1(in[14]), .out(multiplexer_11_out), .sel(shift_by[2]));
  Multiplexer #(.disabled(0), .enable("false")) multiplexer_12 (
    .in0(in[11]), .in1(in[15]), .out(multiplexer_12_out), .sel(shift_by[2]));
  Multiplexer #(.disabled(0), .enable("false")) multiplexer_13 (
    .in0(in[12]), .in1(1'b0), .out(multiplexer_13_out), .sel(shift_by[2]));
  Multiplexer #(.disabled(0), .enable("false")) multiplexer_14 (
    .in0(in[13]), .in1(1'b0), .out(multiplexer_14_out), .sel(shift_by[2]));
  Multiplexer #(.disabled(0), .enable("false")) multiplexer_15 (
    .in0(in[14]), .in1(1'b0), .out(multiplexer_15_out), .sel(shift_by[2]));
  Multiplexer #(.disabled(0), .enable("false")) multiplexer_16 (
    .in0(in[15]), .in1(1'b0), .out(multiplexer_16_out), .sel(shift_by[2]));
  Multiplexer #(.disabled(0), .enable("false")) multiplexer_17 (
    .in0(multiplexer_1_out), .in1(multiplexer_3_out), .out(multiplexer_17_out), .sel(shift_by[1]));
  Multiplexer #(.disabled(0), .enable("false")) multiplexer_18 (
    .in0(multiplexer_2_out), .in1(multiplexer_4_out), .out(multiplexer_18_out), .sel(shift_by[1]));
  Multiplexer #(.disabled(0), .enable("false")) multiplexer_19 (
    .in0(multiplexer_3_out), .in1(multiplexer_5_out), .out(multiplexer_19_out), .sel(shift_by[1]));
  Multiplexer #(.disabled(0), .enable("false")) multiplexer_20 (
    .in0(multiplexer_4_out), .in1(multiplexer_6_out), .out(multiplexer_20_out), .sel(shift_by[1]));
  Multiplexer #(.disabled(0), .enable("false")) multiplexer_21 (
    .in0(multiplexer_5_out), .in1(multiplexer_7_out), .out(multiplexer_21_out), .sel(shift_by[1]));
  Multiplexer #(.disabled(0), .enable("false")) multiplexer_22 (
    .in0(multiplexer_6_out), .in1(multiplexer_8_out), .out(multiplexer_22_out), .sel(shift_by[1]));
  Multiplexer #(.disabled(0), .enable("false")) multiplexer_23 (
    .in0(multiplexer_7_out), .in1(multiplexer_9_out), .out(multiplexer_23_out), .sel(shift_by[1]));
  Multiplexer #(.disabled(0), .enable("false")) multiplexer_24 (
    .in0(multiplexer_8_out), .in1(multiplexer_10_out), .out(multiplexer_24_out), .sel(shift_by[1]));
  Multiplexer #(.disabled(0), .enable("false")) multiplexer_25 (
    .in0(multiplexer_9_out), .in1(multiplexer_11_out), .out(multiplexer_25_out), .sel(shift_by[1]));
  Multiplexer #(.disabled(0), .enable("false")) multiplexer_26 (
    .in0(multiplexer_10_out), .in1(multiplexer_12_out), .out(multiplexer_26_out), .sel(shift_by[1]));
  Multiplexer #(.disabled(0), .enable("false")) multiplexer_27 (
    .in0(multiplexer_11_out), .in1(multiplexer_13_out), .out(multiplexer_27_out), .sel(shift_by[1]));
  Multiplexer #(.disabled(0), .enable("false")) multiplexer_28 (
    .in0(multiplexer_12_out), .in1(multiplexer_14_out), .out(multiplexer_28_out), .sel(shift_by[1]));
  Multiplexer #(.disabled(0), .enable("false")) multiplexer_29 (
    .in0(multiplexer_13_out), .in1(multiplexer_15_out), .out(multiplexer_29_out), .sel(shift_by[1]));
  Multiplexer #(.disabled(0), .enable("false")) multiplexer_30 (
    .in0(multiplexer_14_out), .in1(multiplexer_16_out), .out(multiplexer_30_out), .sel(shift_by[1]));
  Multiplexer #(.disabled(0), .enable("false")) multiplexer_31 (
    .in0(multiplexer_15_out), .in1(1'b0), .out(multiplexer_31_out), .sel(shift_by[1]));
  Multiplexer #(.disabled(0), .enable("false")) multiplexer_32 (
    .in0(multiplexer_16_out), .in1(1'b0), .out(multiplexer_32_out), .sel(shift_by[1]));
  Multiplexer #(.disabled(0), .enable("false")) multiplexer_33 (
    .in0(multiplexer_17_out), .in1(multiplexer_18_out), .out(out[0]), .sel(shift_by[0]));
  Multiplexer #(.disabled(0), .enable("false")) multiplexer_34 (
    .in0(multiplexer_18_out), .in1(multiplexer_19_out), .out(out[1]), .sel(shift_by[0]));
  Multiplexer #(.disabled(0), .enable("false")) multiplexer_35 (
    .in0(multiplexer_19_out), .in1(multiplexer_20_out), .out(out[2]), .sel(shift_by[0]));
  Multiplexer #(.disabled(0), .enable("false")) multiplexer_36 (
    .in0(multiplexer_20_out), .in1(multiplexer_21_out), .out(out[3]), .sel(shift_by[0]));
  Multiplexer #(.disabled(0), .enable("false")) multiplexer_37 (
    .in0(multiplexer_21_out), .in1(multiplexer_22_out), .out(out[4]), .sel(shift_by[0]));
  Multiplexer #(.disabled(0), .enable("false")) multiplexer_38 (
    .in0(multiplexer_22_out), .in1(multiplexer_23_out), .out(out[5]), .sel(shift_by[0]));
  Multiplexer #(.disabled(0), .enable("false")) multiplexer_39 (
    .in0(multiplexer_23_out), .in1(multiplexer_24_out), .out(out[6]), .sel(shift_by[0]));
  Multiplexer #(.disabled(0), .enable("false")) multiplexer_40 (
    .in0(multiplexer_24_out), .in1(multiplexer_25_out), .out(out[7]), .sel(shift_by[0]));
  Multiplexer #(.disabled(0), .enable("false")) multiplexer_41 (
    .in0(multiplexer_25_out), .in1(multiplexer_26_out), .out(out[8]), .sel(shift_by[0]));
  Multiplexer #(.disabled(0), .enable("false")) multiplexer_42 (
    .in0(multiplexer_26_out), .in1(multiplexer_27_out), .out(out[9]), .sel(shift_by[0]));
  Multiplexer #(.disabled(0), .enable("false")) multiplexer_43 (
    .in0(multiplexer_27_out), .in1(multiplexer_28_out), .out(out[10]), .sel(shift_by[0]));
  Multiplexer #(.disabled(0), .enable("false")) multiplexer_44 (
    .in0(multiplexer_28_out), .in1(multiplexer_29_out), .out(out[11]), .sel(shift_by[0]));
  Multiplexer #(.disabled(0), .enable("false")) multiplexer_45 (
    .in0(multiplexer_29_out), .in1(multiplexer_30_out), .out(out[12]), .sel(shift_by[0]));
  Multiplexer #(.disabled(0), .enable("false")) multiplexer_46 (
    .in0(multiplexer_30_out), .in1(multiplexer_31_out), .out(out[13]), .sel(shift_by[0]));
  Multiplexer #(.disabled(0), .enable("false")) multiplexer_47 (
    .in0(multiplexer_31_out), .in1(multiplexer_32_out), .out(out[14]), .sel(shift_by[0]));
  Multiplexer #(.disabled(0), .enable("false")) multiplexer_48 (
    .in0(multiplexer_32_out), .in1(1'b0), .out(out[15]), .sel(shift_by[0]));

  // Other names for the same wires on the sheet: _1 = shift_by[0]; _2 = shift_by[1]; _3 = shift_by[2]
endmodule

module left_logical_shift (
  input  [2:0] shift_by,
  input  [15:0] in,
  output [15:0] out
);

  wire multiplexer_1_out, multiplexer_2_out, multiplexer_3_out, multiplexer_4_out, multiplexer_5_out,
       multiplexer_6_out, multiplexer_7_out, multiplexer_8_out, multiplexer_9_out, multiplexer_10_out,
       multiplexer_11_out, multiplexer_12_out, multiplexer_13_out, multiplexer_14_out, multiplexer_15_out,
       multiplexer_16_out, multiplexer_17_out, multiplexer_18_out, multiplexer_19_out, multiplexer_20_out,
       multiplexer_21_out, multiplexer_22_out, multiplexer_23_out, multiplexer_24_out, multiplexer_25_out,
       multiplexer_26_out, multiplexer_27_out, multiplexer_28_out, multiplexer_29_out, multiplexer_30_out,
       multiplexer_31_out, multiplexer_32_out;

  Multiplexer #(.disabled(0), .enable("false")) multiplexer_1 (
    .in0(in[15]), .in1(in[11]), .out(multiplexer_1_out), .sel(shift_by[2]));
  Multiplexer #(.disabled(0), .enable("false")) multiplexer_2 (
    .in0(in[14]), .in1(in[10]), .out(multiplexer_2_out), .sel(shift_by[2]));
  Multiplexer #(.disabled(0), .enable("false")) multiplexer_3 (
    .in0(in[13]), .in1(in[9]), .out(multiplexer_3_out), .sel(shift_by[2]));
  Multiplexer #(.disabled(0), .enable("false")) multiplexer_4 (
    .in0(in[12]), .in1(in[8]), .out(multiplexer_4_out), .sel(shift_by[2]));
  Multiplexer #(.disabled(0), .enable("false")) multiplexer_5 (
    .in0(in[11]), .in1(in[7]), .out(multiplexer_5_out), .sel(shift_by[2]));
  Multiplexer #(.disabled(0), .enable("false")) multiplexer_6 (
    .in0(in[10]), .in1(in[6]), .out(multiplexer_6_out), .sel(shift_by[2]));
  Multiplexer #(.disabled(0), .enable("false")) multiplexer_7 (
    .in0(in[9]), .in1(in[5]), .out(multiplexer_7_out), .sel(shift_by[2]));
  Multiplexer #(.disabled(0), .enable("false")) multiplexer_8 (
    .in0(in[8]), .in1(in[4]), .out(multiplexer_8_out), .sel(shift_by[2]));
  Multiplexer #(.disabled(0), .enable("false")) multiplexer_9 (
    .in0(in[7]), .in1(in[3]), .out(multiplexer_9_out), .sel(shift_by[2]));
  Multiplexer #(.disabled(0), .enable("false")) multiplexer_10 (
    .in0(in[6]), .in1(in[2]), .out(multiplexer_10_out), .sel(shift_by[2]));
  Multiplexer #(.disabled(0), .enable("false")) multiplexer_11 (
    .in0(in[5]), .in1(in[1]), .out(multiplexer_11_out), .sel(shift_by[2]));
  Multiplexer #(.disabled(0), .enable("false")) multiplexer_12 (
    .in0(in[4]), .in1(in[0]), .out(multiplexer_12_out), .sel(shift_by[2]));
  Multiplexer #(.disabled(0), .enable("false")) multiplexer_13 (
    .in0(in[3]), .in1(1'b0), .out(multiplexer_13_out), .sel(shift_by[2]));
  Multiplexer #(.disabled(0), .enable("false")) multiplexer_14 (
    .in0(in[2]), .in1(1'b0), .out(multiplexer_14_out), .sel(shift_by[2]));
  Multiplexer #(.disabled(0), .enable("false")) multiplexer_15 (
    .in0(in[1]), .in1(1'b0), .out(multiplexer_15_out), .sel(shift_by[2]));
  Multiplexer #(.disabled(0), .enable("false")) multiplexer_16 (
    .in0(in[0]), .in1(1'b0), .out(multiplexer_16_out), .sel(shift_by[2]));
  Multiplexer #(.disabled(0), .enable("false")) multiplexer_17 (
    .in0(multiplexer_1_out), .in1(multiplexer_3_out), .out(multiplexer_17_out), .sel(shift_by[1]));
  Multiplexer #(.disabled(0), .enable("false")) multiplexer_18 (
    .in0(multiplexer_2_out), .in1(multiplexer_4_out), .out(multiplexer_18_out), .sel(shift_by[1]));
  Multiplexer #(.disabled(0), .enable("false")) multiplexer_19 (
    .in0(multiplexer_3_out), .in1(multiplexer_5_out), .out(multiplexer_19_out), .sel(shift_by[1]));
  Multiplexer #(.disabled(0), .enable("false")) multiplexer_20 (
    .in0(multiplexer_4_out), .in1(multiplexer_6_out), .out(multiplexer_20_out), .sel(shift_by[1]));
  Multiplexer #(.disabled(0), .enable("false")) multiplexer_21 (
    .in0(multiplexer_5_out), .in1(multiplexer_7_out), .out(multiplexer_21_out), .sel(shift_by[1]));
  Multiplexer #(.disabled(0), .enable("false")) multiplexer_22 (
    .in0(multiplexer_6_out), .in1(multiplexer_8_out), .out(multiplexer_22_out), .sel(shift_by[1]));
  Multiplexer #(.disabled(0), .enable("false")) multiplexer_23 (
    .in0(multiplexer_7_out), .in1(multiplexer_9_out), .out(multiplexer_23_out), .sel(shift_by[1]));
  Multiplexer #(.disabled(0), .enable("false")) multiplexer_24 (
    .in0(multiplexer_8_out), .in1(multiplexer_10_out), .out(multiplexer_24_out), .sel(shift_by[1]));
  Multiplexer #(.disabled(0), .enable("false")) multiplexer_25 (
    .in0(multiplexer_9_out), .in1(multiplexer_11_out), .out(multiplexer_25_out), .sel(shift_by[1]));
  Multiplexer #(.disabled(0), .enable("false")) multiplexer_26 (
    .in0(multiplexer_10_out), .in1(multiplexer_12_out), .out(multiplexer_26_out), .sel(shift_by[1]));
  Multiplexer #(.disabled(0), .enable("false")) multiplexer_27 (
    .in0(multiplexer_11_out), .in1(multiplexer_13_out), .out(multiplexer_27_out), .sel(shift_by[1]));
  Multiplexer #(.disabled(0), .enable("false")) multiplexer_28 (
    .in0(multiplexer_12_out), .in1(multiplexer_14_out), .out(multiplexer_28_out), .sel(shift_by[1]));
  Multiplexer #(.disabled(0), .enable("false")) multiplexer_29 (
    .in0(multiplexer_13_out), .in1(multiplexer_15_out), .out(multiplexer_29_out), .sel(shift_by[1]));
  Multiplexer #(.disabled(0), .enable("false")) multiplexer_30 (
    .in0(multiplexer_14_out), .in1(multiplexer_16_out), .out(multiplexer_30_out), .sel(shift_by[1]));
  Multiplexer #(.disabled(0), .enable("false")) multiplexer_31 (
    .in0(multiplexer_15_out), .in1(1'b0), .out(multiplexer_31_out), .sel(shift_by[1]));
  Multiplexer #(.disabled(0), .enable("false")) multiplexer_32 (
    .in0(multiplexer_16_out), .in1(1'b0), .out(multiplexer_32_out), .sel(shift_by[1]));
  Multiplexer #(.disabled(0), .enable("false")) multiplexer_33 (
    .in0(multiplexer_17_out), .in1(multiplexer_18_out), .out(out[15]), .sel(shift_by[0]));
  Multiplexer #(.disabled(0), .enable("false")) multiplexer_34 (
    .in0(multiplexer_18_out), .in1(multiplexer_19_out), .out(out[14]), .sel(shift_by[0]));
  Multiplexer #(.disabled(0), .enable("false")) multiplexer_35 (
    .in0(multiplexer_19_out), .in1(multiplexer_20_out), .out(out[13]), .sel(shift_by[0]));
  Multiplexer #(.disabled(0), .enable("false")) multiplexer_36 (
    .in0(multiplexer_20_out), .in1(multiplexer_21_out), .out(out[12]), .sel(shift_by[0]));
  Multiplexer #(.disabled(0), .enable("false")) multiplexer_37 (
    .in0(multiplexer_21_out), .in1(multiplexer_22_out), .out(out[11]), .sel(shift_by[0]));
  Multiplexer #(.disabled(0), .enable("false")) multiplexer_38 (
    .in0(multiplexer_22_out), .in1(multiplexer_23_out), .out(out[10]), .sel(shift_by[0]));
  Multiplexer #(.disabled(0), .enable("false")) multiplexer_39 (
    .in0(multiplexer_23_out), .in1(multiplexer_24_out), .out(out[9]), .sel(shift_by[0]));
  Multiplexer #(.disabled(0), .enable("false")) multiplexer_40 (
    .in0(multiplexer_24_out), .in1(multiplexer_25_out), .out(out[8]), .sel(shift_by[0]));
  Multiplexer #(.disabled(0), .enable("false")) multiplexer_41 (
    .in0(multiplexer_25_out), .in1(multiplexer_26_out), .out(out[7]), .sel(shift_by[0]));
  Multiplexer #(.disabled(0), .enable("false")) multiplexer_42 (
    .in0(multiplexer_26_out), .in1(multiplexer_27_out), .out(out[6]), .sel(shift_by[0]));
  Multiplexer #(.disabled(0), .enable("false")) multiplexer_43 (
    .in0(multiplexer_27_out), .in1(multiplexer_28_out), .out(out[5]), .sel(shift_by[0]));
  Multiplexer #(.disabled(0), .enable("false")) multiplexer_44 (
    .in0(multiplexer_28_out), .in1(multiplexer_29_out), .out(out[4]), .sel(shift_by[0]));
  Multiplexer #(.disabled(0), .enable("false")) multiplexer_45 (
    .in0(multiplexer_29_out), .in1(multiplexer_30_out), .out(out[3]), .sel(shift_by[0]));
  Multiplexer #(.disabled(0), .enable("false")) multiplexer_46 (
    .in0(multiplexer_30_out), .in1(multiplexer_31_out), .out(out[2]), .sel(shift_by[0]));
  Multiplexer #(.disabled(0), .enable("false")) multiplexer_47 (
    .in0(multiplexer_31_out), .in1(multiplexer_32_out), .out(out[1]), .sel(shift_by[0]));
  Multiplexer #(.disabled(0), .enable("false")) multiplexer_48 (
    .in0(multiplexer_32_out), .in1(1'b0), .out(out[0]), .sel(shift_by[0]));

  // Other names for the same wires on the sheet: _1 = shift_by[0]; _2 = shift_by[1]; _3 = shift_by[2]
endmodule

module pc_1 (
  input  [15:0] pc,
  output [15:0] pc_4
);

  adder adder_1 (.B(16'h1), .sub(1'b0), .A(pc), .result(pc_4));  // open: ovf
endmodule

module Instruction_Decode (
  input  [15:0] instruction,
  output [11:0] Address,
  output [5:0] Immediate,
  output [2:0] shamt,
  output [2:0] Rd,
  output [2:0] Rt,
  output [2:0] Rs,
  output [3:0] opcode
);


  assign Address = instruction[11:0];
  assign Immediate = instruction[5:0];
  assign opcode = instruction[15:12];
  assign Rd = instruction[5:3];
  assign Rs = instruction[11:9];
  assign Rt = instruction[8:6];
  assign shamt = instruction[2:0];
endmodule

module control (
  input  [3:0] Opcode,
  output RWE,
  output DMWe,
  output RWd,
  output JP,
  output \input ,
  output \output ,
  output jal,
  output jr,
  output bne,
  output blt,
  output ALUinB,
  output [2:0] ALUop,
  output Rdst
);

  wire add, addi, \not , or_3_out, sll, srl, sub, \xor ;

  or or_1 (RWE, add, addi, sub, \not , \xor , sll, srl, RWd, jal, \input );
  or or_2 (ALUinB, addi, RWd, DMWe);
  Decoder #(.select(4), .disabled(0)) decoder_1 (
    .out0(add), .out1(addi), .out2(sub), .out3(\not ), .out4(\xor ), .out5(sll), .out6(srl), .out7(RWd),
    .out8(DMWe), .out9(bne), .out10(blt), .out11(JP), .out12(jr), .out13(jal), .out14(\input ),
    .out15(\output ), .sel(Opcode));  // open: en
  or or_3 (or_3_out, addi, DMWe, RWd, add);
  // Priority_Encoder priority_encoder_1: pin names not known; wires that end beside it: or_3_out, sub, \not , \xor , ALUop, sll, srl
  or or_4 (Rdst, add, \not , sll, \xor , srl, sub);

  // Other names for the same wires on the sheet: j = JP; lw = RWd; sw = DMWe
endmodule

// Input Reader
module inputReader (
  input  [6:0] read_Input,
  input  Available,
  output [15:0] Formatted_Read
);

  not not_1 (Formatted_Read[7], Available);

  assign {Formatted_Read[15:8], Formatted_Read[6:0]} = {{8{1'b0}}, read_Input};
endmodule

module displayformatter (
  input  [15:0] rs,
  output [6:0] formatted_display
);


  assign formatted_display = rs[6:0];
endmodule

module address_manipulator (
  input  [15:0] addr12,
  input  [15:0] PC,
  output [15:0] out_3
);


  assign out_3 = {PC[15:12], addr12[11:0]};
endmodule
